# Fritzing sketch VH Arduino Wiring (saved by Fritzing 0.9.3b)
breadboards: 1

parts:
  Part1 = Arduino Uno (Rev3)
  J1 = Infrared Proximity Sensor
  LED1 = LED - 5mm [color="Red (633nm)" package="5 mm [THT]"]
  LED2 = LED - 5mm [color="Red (633nm)" package="5 mm [THT]"]
  J2 = Basic Servo

nets:
  N1: Part1.D8, Part1.D12/MISO, J1.Vout, LED1.cathode, LED2.cathode, J2.pulse
  N2: Part1.D7, J1.GND
  5V: Part1.5V, J2.vcc
  GND: Part1.GND, J2.gnd
  N3: LED1.anode, LED2.anode

notes:
  It is an ultrasonic sensor, not an IR sensor
